# Fritzing sketch Sketch 1 (saved by Fritzing 0.9.3b)
breadboards: 1

parts:
  Part1 = Arduino Uno (Rev3)
  U1 = MLX90614 [package=to-39]
  e-radionica1 = TCS230 Color Sensor [part_number=101209]
  HC-SR04_Sensor_1 = HC-SR04 Ultrasonic Distance Sensor
  Part2 = Bluetooth HC-05 Macho
  R1 = Resistor [tolerance=±20% resistance=1k package=THT]
  R2 = Resistor [tolerance=±5% resistance=2.2k package=THT]
  U2 = TCRT5000 [package=THT]
  U3 = TCRT5000 [package=THT]
  R3 = Resistor [tolerance=±5% resistance=330 package=THT]
  R4 = Resistor [tolerance=±5% resistance=10k package=THT]
  R5 = Resistor [tolerance=±5% resistance=330 package=THT]  # not connected
  R6 = Resistor [tolerance=±5% resistance=10k package=THT]

nets:
  N1: Part1.A4/SDA, U1.VDD
  N2: Part1.A5/SCL, U1.PWM_SDA
  N3: Part1.D8, e-radionica1.S1
  N4: Part1.D9_PWM, e-radionica1.S0
  N5: Part1.D10_PWM/SS, e-radionica1.Out
  N6: Part1.D11_PWM/MOSI, e-radionica1.S3
  N7: Part1.D12/MISO, e-radionica1.S2
  N8: Part1.D2, Part2.TXD
  N9: Part1.D3_PWM, R1.Pin_1
  N10: Part1.D4, HC-SR04_Sensor_1.TRIG
  N11: Part1.D5_PWM, HC-SR04_Sensor_1.ECHO
  N12: Part1.D6_PWM, U2.Pin_4, R6.Pin_0
  N13: Part1.D7, U3.Pin_4, R4.Pin_0
  VCC: Part1.5V, U1.SCL_VZ, U1.VSS, e-radionica1.Vcc, HC-SR04_Sensor_1.VCC, Part2.VCC, R3.Pin_0, R4.Pin_1, R6.Pin_1
  GND: Part1.GND, e-radionica1.Gnd, e-radionica1.OE, HC-SR04_Sensor_1.GND, Part2.GND, R2.Pin_0, U2.Pin_2, U2.Pin_3, U3.Pin_2, U3.Pin_3
  N14: Part2.RXD, R1.Pin_0, R2.Pin_1
  N15: U3.Pin_1, R3.Pin_1

custom parts:
  TCS230 Color Sensor: TCS230
  TCRT5000: TCRT5000 optical reflective sensor
